# Fritzing sketch fuglekafeen (saved by Fritzing 0.9.2b)
circuit board: 8.46667cm x 5.64444cm
breadboards: 1

parts:
  Raspberry_Pi1 = Raspberry Pi B+
  IC1 = MCP3008 8-channel 10-bit ADC [part_number=MCP3008]
  R1 = Photocell (LDR) [package=THT]
  R2 = Resistor [tolerance=±5% resistance=10k package="2010 [SMD]"]
  R3 = Temperature Sensor (Thermistor) [thermistor_type=NTC package=THT]
  R4 = Resistor [tolerance=±5% resistance=10k package="2010 [SMD]"]

nets (from the breadboard view):
  3V3: Raspberry_Pi1.3v3, Raspberry_Pi1.3V3, IC1.no_name_yet#3, IC1.no_name_yet#15, IC1.no_name_yet#16, R2.Pin_0, R4.Pin_1
  N1: Raspberry_Pi1.GPIO10, IC1.no_name_yet#11
  N2: Raspberry_Pi1.GPIO9, IC1.no_name_yet#12
  N3: Raspberry_Pi1.GPIO11, IC1.no_name_yet#13
  N4: Raspberry_Pi1.GND, IC1.no_name_yet#9, IC1.no_name_yet#14, R1.pin_0, R3.pin_1
  N5: Raspberry_Pi1.GPIO8, IC1.no_name_yet#10
  N6: IC1.no_name_yet#1, R1.pin_1, R2.Pin_1
  N7: IC1.no_name_yet#2, R3.pin_0, R4.Pin_0
